// Logisim project adder.circ as structural Verilog: 1 circuit, main circuit main
module main (
);

  wire and_1_out, and_2_out, and_3_out, and_4_out, or_1_out, undriven, undriven_2, undriven_3, undriven_4,
       undriven_5, xor_1_out, xor_2_out;

  and and_1 (and_1_out, undriven, undriven_2);
  xor xor_1 (xor_1_out, undriven, undriven_2);
  and and_2 (and_2_out, undriven_3, undriven_4);
  and and_3 (and_3_out, undriven_3, undriven_5);
  or or_1 (or_1_out, and_2_out, and_3_out, and_4_out);
  and and_4 (and_4_out, undriven_4, undriven_5);
  ExactlyOne xor_2 (.out(xor_2_out), .in0(undriven_3), .in1(undriven_4), .in2(undriven_5));

  // Notes on the sheet:
  //   b
  //   a
  //   Cout
  //   f
  //   b
  //   a
  //   Cin
  //   Cout
  //   f
endmodule
