// Logisim project comperator.circ as structural Verilog: 1 circuit, main circuit main
module main (
);

  wire and_1_out, and_2_out, and_3_out, not_1_out, not_2_out, or_1_out, or_2_out, undriven, undriven_2,
       undriven_3, undriven_4, xnor_1_out;

  not not_1 (not_1_out, undriven_4);
  and and_1 (and_1_out, undriven_3, not_1_out, undriven_3);
  not not_2 (not_2_out, undriven_3);
  and and_2 (and_2_out, undriven_4, not_2_out, undriven_3);
  xnor xnor_1 (xnor_1_out, undriven_4, undriven_3);
  or or_1 (or_1_out, undriven, and_1_out);
  or or_2 (or_2_out, undriven_2, and_2_out);
  and and_3 (and_3_out, undriven_3, xnor_1_out);

  // Notes on the sheet:
  //   in_gt
  //   in_eq
  //   in_lt
  //   b
  //   a
  //   out_gt
  //   out_lt
  //   out_eq
endmodule
