// Logisim project multipler.circ as structural Verilog: 1 circuit, main circuit main
module main (
);

  wire and_1_out, and_2_out, and_3_out, and_4_out, and_5_out, and_6_out, and_7_out, and_8_out, and_9_out,
       undriven, undriven_2, undriven_3, undriven_4, undriven_5, undriven_6;

  and and_1 (and_1_out, undriven, undriven_4);
  and and_2 (and_2_out, undriven_2, undriven_4);
  and and_3 (and_3_out, undriven_3, undriven_4);
  and and_4 (and_4_out, undriven, undriven_5);
  and and_5 (and_5_out, undriven_2, undriven_5);
  and and_6 (and_6_out, undriven_3, undriven_5);
  and and_7 (and_7_out, undriven, undriven_6);
  and and_8 (and_8_out, undriven_2, undriven_6);
  and and_9 (and_9_out, undriven_3, undriven_6);

  // Notes on the sheet:
  //   x3
  //   y2
  //   y1
  //   y0
  //   x2
  //   x1
  //   0
  //   0
  //   0
  //   0
endmodule
