// Logisim project substractor.circ as structural Verilog: 1 circuit, main circuit main
module main (
);

  wire and_1_out, and_2_out, and_3_out, not_1_out, not_2_out, not_3_out, or_1_out, undriven, undriven_2,
       undriven_3, undriven_4, undriven_5, xor_1_out, xor_2_out, xor_3_out;

  xor xor_1 (xor_1_out, undriven, undriven_2);
  not not_1 (not_1_out, undriven);
  and and_1 (and_1_out, not_1_out, undriven_2);
  xor xor_2 (xor_2_out, undriven_3, xor_3_out);
  xor xor_3 (xor_3_out, undriven_4, undriven_5);
  not not_2 (not_2_out, xor_3_out);
  and and_2 (and_2_out, not_2_out, undriven_3);
  not not_3 (not_3_out, undriven_5);
  and and_3 (and_3_out, undriven_4, not_3_out);
  or or_1 (or_1_out, and_2_out, and_3_out);

  // Notes on the sheet:
  //   y
  //   x
  //   Difference
  //   Bout
  //   y
  //   Bin
  //   Difference
  //   x
  //   Bout
endmodule
